# Fritzing sketch final_prototype_bms (saved by Fritzing 0.9.3b)
breadboards: 1
stripboards: 1

parts:
  U1 = atmega328 [package=dip]
  C1 = Ceramic Capacitor [capacitance=22µF package="200 mil [THT, multilayer]"]
  C2 = Ceramic Capacitor [capacitance=22µF package="200 mil [THT, multilayer]"]  # not connected
  XTAL1 = Crystal [frequency="16 Mhz" package=SMD]
  R1 = Resistor [tolerance=±5% resistance=10k package=THT]
  C3 = Electrolytic Capacitor [capacitance=10µF package="100 mil [THT, electrolytic]"]
  LED1 = LED - 5mm [color="Red (633nm)" package="5 mm [THT]"]
  LED2 = LED - 5mm [color="Red (633nm)" package="5 mm [THT]"]
  LED3 = LED - 5mm [color="Red (633nm)" package="5 mm [THT]"]
  LED4 = LED - 5mm [color="Red (633nm)" package="5 mm [THT]"]
  R2 = Resistor [tolerance=±5% resistance=220 package=THT]
  R3 = Resistor [tolerance=±5% resistance=220 package=THT]
  R4 = Resistor [tolerance=±5% resistance=220 package=THT]
  R5 = Resistor [tolerance=±5% resistance=220 package=THT]
  S1 = Pushbutton [package="[THT]"]
  S2 = Pushbutton [package="[THT]"]
  VCC1 = Battery
  VCC2 = Battery
  VCC3 = Battery
  R8 = Resistor [tolerance=±5% resistance=10k package=THT]
  R9 = Resistor [tolerance=±5% resistance=10k package=THT]
  R10 = Resistor [tolerance=±5% resistance=5k package=THT]
  R11 = Resistor [tolerance=±5% resistance=10k package=THT]
  R12 = Resistor [tolerance=±5% resistance=10k package=THT]
  J1 = female alternating pin header, 4 pins [form="♀ (female)"]
  J2 = female alternating pin header, 6 pins [form="♀ (female)"]
  C13 = Ceramic Capacitor [capacitance=100nF package="0805 [SMD, multilayer]"]
  J3 = screw terminal, 2 pins

nets:
  N1: U1.RESET, R1.Pin_1, S1.Pin_1, S1.Pin_2, C13.0
  N2: U1.D0_(RX), J2.pin3
  N3: U1.D1_(TX), J2.pin2
  N4: U1.D2, S2.Pin_1, S2.Pin_2
  N5: U1.VCC, U1.AVCC, U1.AREF, U1.A2, R1.Pin_0, C3.+, VCC1.+, VCC2.-, R8.Pin_1, J1.pin4, J2.pin4
  N6: U1.GND, C1.1, C3.-, R2.Pin_1, R3.Pin_1, R4.Pin_1, R5.Pin_1, S1.Pin_3, S1.Pin_4, S2.Pin_3, S2.Pin_4, VCC1.-, R8.Pin_0, R9.Pin_0, J1.pin1, J2.pin5, J2.pin6, J3.pin1
  N7: U1.XLAT1, XTAL1.pin_0
  N8: U1.XLAT2, C1.0, XTAL1.pin_1
  N9: U1.D7, J1.pin2
  N10: U1.D8, J1.pin3
  N11: U1.D9_(PWM), LED4.anode
  N12: U1.D10_(PWM), LED3.anode
  N13: U1.D11_(PWM), LED2.anode
  N14: U1.D12, LED1.anode
  N15: U1.A0, R10.Pin_1, R12.Pin_1
  N16: U1.A1, R9.Pin_1
  N17: U1.A4, R11.Pin_1
  N18: LED1.cathode, R2.Pin_0
  N19: LED2.cathode, R3.Pin_0
  N20: LED3.cathode, R4.Pin_0
  N21: LED4.cathode, R5.Pin_0
  N22: VCC2.+, VCC3.-, R11.Pin_0
  N23: VCC3.+, R12.Pin_0, J3.pin2
  N24: J2.pin1, C13.1
