# Fritzing sketch test_protoboard (saved by Fritzing 0.9.3b)
stripboards: 3

parts:
  R1 = Resistor [tolerance=±5% resistance=10k package=THT]
  R2 = Resistor [tolerance=±5% resistance=10k package=THT]
  R3 = Resistor [tolerance=±5% resistance=10k package=THT]
  R5 = Resistor [tolerance=±5% resistance=10k package=THT]
  C3 = Electrolytic Capacitor [capacitance=1µF voltage=7 package="100 mil [THT, electrolytic]"]
  LED1 = LED - 5mm [color="Red (633nm)" package="5 mm [THT]"]
  LED2 = LED - 5mm [color="Red (633nm)" package="5 mm [THT]"]
  LED3 = LED - 5mm [color="Red (633nm)" package="5 mm [THT]"]
  LED4 = LED - 5mm [color="Red (633nm)" package="5 mm [THT]"]
  R6 = Resistor [tolerance=±5% resistance=330 package=THT]
  R7 = Resistor [tolerance=±5% resistance=330 package=THT]
  R9 = Resistor [tolerance=±5% resistance=330 package=THT]
  R8 = Resistor [tolerance=±5% resistance=330 package=THT]
  R10 = Resistor [tolerance=±5% resistance=10k package=THT]
  J1 = male pin header, 4 pins [form="♂ (male)"]
  J2 = female pin header, 4 pins [form="♀ (female)"]
  J3 = female pin header, 4 pins [form="♀ (female)"]
  C4 = Electrolytic Capacitor [capacitance=1µF voltage=7 package="100 mil [THT, electrolytic]"]
  C5 = Electrolytic Capacitor [capacitance=1µF voltage=7 package="100 mil [THT, electrolytic]"]
  S1 = Pushbutton [package="[THT]"]
  J4 = female pin header, 6 pins [form="♀ (female)"]

nets:
  N1: R1.Pin_0, R3.Pin_0, R10.Pin_0, J2.pin1, J3.pin1
  N2: R1.Pin_1, R2.Pin_0, R10.Pin_1, J3.pin2
  N3: R2.Pin_1, J2.pin2
  N4: R3.Pin_1, R5.Pin_0, J3.pin3
  N5: R5.Pin_1, J2.pin3
  N6: C3.-, J1.pin2, C5.+
  N7: C3.+, J1.pin3, C4.-
  N8: LED1.cathode, LED2.cathode, LED3.cathode, LED4.cathode, S1.Pin_3, S1.Pin_4, J4.pin1
  N9: LED1.anode, R9.Pin_0
  N10: LED2.anode, R6.Pin_0
  N11: LED3.anode, R7.Pin_0
  N12: LED4.anode, R8.Pin_0
  N13: R6.Pin_1, J4.pin3
  N14: R7.Pin_1, J4.pin4
  N15: R9.Pin_1, J4.pin2
  N16: R8.Pin_1, J4.pin5
  N17: J1.pin1, C5.-
  N18: J1.pin4, C4.+
  N19: J2.pin4, J3.pin4
  N20: S1.Pin_1, S1.Pin_2, J4.pin6
